# Fritzing sketch cift-motor (saved by Fritzing 0.9.3b)
breadboards: 1

parts:
  Right_Motor = DC Motor
  Arduino_UNO1 = Arduino Uno (Rev3)
  VCC1 = Battery block 9V  # not connected
  L298N_Module = H-Bridge with L298N
  VCC2 = Battery block 9V
  Right_Motor1 = DC Motor

nets:
  N1: Right_Motor.pin_1, L298N_Module.M2-02
  N2: Right_Motor.pin_2, L298N_Module.M2-01
  N3: Arduino_UNO1.D8, L298N_Module.IN2
  N4: Arduino_UNO1.D9_PWM, L298N_Module.IN1
  N5: Arduino_UNO1.D11_PWM/MOSI, L298N_Module.ENA
  GND: Arduino_UNO1.GND, L298N_Module.GND, VCC2.-
  N6: Arduino_UNO1.D3_PWM, L298N_Module.ENB
  N7: Arduino_UNO1.D6_PWM, L298N_Module.IN4
  N8: Arduino_UNO1.D7, L298N_Module.IN3
  N9: L298N_Module.12V, VCC2.+
  N10: L298N_Module.M1-01, Right_Motor1.pin_2
  N11: L298N_Module.M1-02, Right_Motor1.pin_1

notes:
  L298N
  Motor Sürücü

custom parts:
  H-Bridge with L298N: h-bridge

// code stored in the sketch: 2FotoResistencias2Leds2Motores.fzz.ino
// Autor  Samuel  Huerta  ITMA

//  asigna  los  pines del  driver  con los del arduino
int IN1 = 11;
int IN2 = 10;
int IN3 = 9;
int IN4 = 8;
//-----------------
int LED2 =2;
int LED3= 3;
int LDR0 = A0;
int LDR1 = A1;
int threshold0 = 300;//  importante  calibrar  segun  el area  a trabajar  
int threshold1 = 300;

void setup() {    //  salida de  los  pines para leds
   ///---------------------------
 pinMode(LDR0, INPUT);
 pinMode(LDR1, INPUT);
 pinMode(LED2, OUTPUT);
 pinMode(LED3, OUTPUT);
   //   salidas para el  driver
  pinMode (IN1, OUTPUT); //11
  pinMode (IN2, OUTPUT);// 10
  pinMode (IN3, OUTPUT); //9
  pinMode (IN4, OUTPUT); //8
}
void loop() {   
                  //_--------------------Izquierda
 int sensor0 = analogRead(LDR0);
  if (sensor0 >= threshold0) {
    digitalWrite(LED2, HIGH);
    digitalWrite (IN1, HIGH);   
    digitalWrite (IN2, LOW);
    delay(100);
    } else {
    digitalWrite(LED2, LOW);
    digitalWrite (IN1, LOW);
        }       
    //--------------------A1
 int sensor1 = analogRead(LDR1);
  if (sensor1 >= threshold1) {
     digitalWrite(LED3,HIGH);
    digitalWrite (IN3, HIGH);   
    digitalWrite (IN4, LOW);
    delay(100);
    } else {
    digitalWrite(LED3,LOW);
    digitalWrite (IN3, LOW);
    
        }   
 
}



























// Autor  Samuel  Huerta  ITMA
